# Fritzing sketch animatronico-linguo-1.1 (saved by Fritzing 0.9.3b)

parts:
  J1 = Basic Servo
  J2 = Basic Servo
  J3 = Basic Servo
  J4 = Basic Servo
  J6 = Basic Servo
  Componente3 = Adafruit PCA9685 PWM/Servo Breakout [part_number=815]
  J7 = Basic Servo
  VCC1 = 4 x AAA Battery Mount  # not connected
  MH-ET_LIVE_ESP32_DEVKIT1 = MH-ET LIVE ESP32 DEVKIT 38 pins  # not connected
  M1 = Stepper Motor - Bipolar  # not connected
  TP1 = TP4056 [chip_label=TP4056 package="DIP (Dual Inline) [THT]"]  # not connected
  Componente4 = Adafruit APDS-9960 [part_number="Adafruit #3595"]  # not connected
  Componente5 = Bluetooth HC-06  # not connected

nets:
  GND: J1.gnd, J2.gnd, J3.gnd, J4.gnd, J6.gnd, Componente3.GND, J7.gnd
  VCC: J1.vcc, J2.vcc, J3.vcc, J4.vcc, J6.vcc, Componente3.5.0V, J7.vcc
  N1: J1.pulse, Componente3.PWM3
  N2: J2.pulse, Componente3.PWM4
  N3: J3.pulse, Componente3.PWM5
  N4: J4.pulse, Componente3.PWM0
  N5: J6.pulse, Componente3.PWM2
  N6: Componente3.PWM1, J7.pulse

custom parts:
  Adafruit PCA9685 PWM/Servo Breakout: Using only two pins, control 16 free-running PWM outputs! I2C-controlled PWM driver with a built in clock. Unlike the TLC5940 family, you do not need to continuously send it signal tying up your microcontroller, its completely free running! 5V compliant, which means you can control it from a 3.3V microcontroller and still safely drive up to 6V outputs (this is good for when you want to control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
  MH-ET LIVE ESP32 DEVKIT 38 pins: http://mh.nodebb.com/topic/2/mh-et-live-esp32-devkit
  TP4056: A DIP stand-in part for whatever IC you want. With 6 pins on a 300mil dual inline package (DIP) footprint.
  Adafruit APDS-9960: The APDS9960 from Avago Technologies has an integrated IR LED and driver, along with four directional photodiodes that sense reflected IR energy from the LED. It's proximity detection feature allows it to measure the distance an object is from the front of the sensor (up to a few centimeters) with 8 bit resolution. Since there are four IR sensors, you can measure the changes in light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
