# Fritzing sketch Esquematico_Linguo (saved by Fritzing 1.0.4)

parts:
  Componente1 = Adafruit PCA9685 PWM/Servo Breakout [part_number=815]
  MH-ET_LIVE_ESP32_DEVKIT1 = MH-ET LIVE ESP32 DEVKIT 38 pins
  Componente2 = Adafruit APDS-9960 [part_number="Adafruit #3595"]
  J2 = Basic Servo
  J3 = Basic Servo
  J4 = Basic Servo
  J5 = Basic Servo
  J6 = Basic Servo
  J1 = Basic Servo
  BAT1 = BC9VPC [package=bc9vpc]

nets:
  N1: Componente1.PWRIN, BAT1.V+
  GND: Componente1.GND, MH-ET_LIVE_ESP32_DEVKIT1.GND#64, J2.gnd, J3.gnd, J4.gnd, J5.gnd, J6.gnd, J1.gnd, BAT1.V-
  N2: Componente1.PWM5, J5.pulse
  VCC: Componente1.5.0V, J2.vcc, J3.vcc, J4.vcc, J5.vcc, J6.vcc, J1.vcc
  N3: Componente1.PWM4, J4.pulse
  N4: Componente1.PWM3, J6.pulse
  N5: Componente1.PWM2, J3.pulse
  N6: Componente1.PWM1, J2.pulse
  N7: Componente1.PWM0, J1.pulse
  VCC_2: Componente1.VCC, MH-ET_LIVE_ESP32_DEVKIT1.3V3, Componente2.3.3V
  N8: Componente1.SDA, MH-ET_LIVE_ESP32_DEVKIT1.IO21, Componente2.SDA
  N9: Componente1.SCL, MH-ET_LIVE_ESP32_DEVKIT1.IO22, Componente2.SCL
  N10: MH-ET_LIVE_ESP32_DEVKIT1.GND#58, Componente2.GND
  5V: MH-ET_LIVE_ESP32_DEVKIT1.5V, Componente2.VIN

custom parts:
  Adafruit PCA9685 PWM/Servo Breakout: Using only two pins, control 16 free-running PWM outputs! I2C-controlled PWM driver with a built in clock. Unlike the TLC5940 family, you do not need to continuously send it signal tying up your microcontroller, its completely free running! 5V compliant, which means you can control it from a 3.3V microcontroller and still safely drive up to 6V outputs (this is good for when you want to control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
  MH-ET LIVE ESP32 DEVKIT 38 pins: http://mh.nodebb.com/topic/2/mh-et-live-esp32-devkit
  Adafruit APDS-9960: The APDS9960 from Avago Technologies has an integrated IR LED and driver, along with four directional photodiodes that sense reflected IR energy from the LED. It's proximity detection feature allows it to measure the distance an object is from the front of the sensor (up to a few centimeters) with 8 bit resolution. Since there are four IR sensors, you can measure the changes in light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
